# Fritzing sketch FUMZFV6IVA4M4VP (saved by Fritzing 0.9.2b)
circuit board: 4.4cm x 4.4cm
breadboards: 1

parts:
  part = Arduino Nano (Rev3.0)
  part_2 = MPU-6050 Board GY-521 [form="♀ (female)" package=THT]
  part_3 = female pin header, 11 pins [form="♀ (female)"]
  part_4 = female pin header, 2 pins [form="♀ (female)"]
  part_5 = female pin header, 1 pin [form="♀ (female)"]
  part_6 = female pin header, 1 pin [form="♀ (female)"]
  part_7 = female pin header, 11 pins [form="♀ (female)"]
  part_8 = female pin header, 11 pins [form="♀ (female)"]

nets:
  N1: part.D1/TX, part_4.pin1
  N2: part.D0/RX, part_4.pin2
  N3: part.GND, part_2.pin2, part_6.pin1, part_8.pin1, part_8.pin2, part_8.pin3, part_8.pin4, part_8.pin5, part_8.pin6, part_8.pin7, part_8.pin8, part_8.pin9, part_8.pin10, part_8.pin11
  N4: part.D2, part_3.pin1
  N5: part.D3, part_3.pin2
  N6: part.D4, part_3.pin3
  N7: part.D5, part_3.pin4
  N8: part.D6, part_3.pin5
  N9: part.D7, part_3.pin6
  N10: part.D8, part_3.pin7
  N11: part.D9, part_3.pin8
  N12: part.D10, part_3.pin9
  N13: part.D11/MOSI, part_3.pin10
  N14: part.D12/MISO, part_3.pin11
  N15: part.VIN, part_2.pin1, part_5.pin1, part_7.pin1, part_7.pin2, part_7.pin3, part_7.pin4, part_7.pin5, part_7.pin6, part_7.pin7, part_7.pin8, part_7.pin9, part_7.pin10, part_7.pin11
  N16: part.A5, part_2.pin3
  N17: part.A4, part_2.pin4

notes:
  GND
  5V
  D2
  - + Sig
  D3
  D4
  D5
  D6
  D7
  D8
  D9
  D10
  D11
  D12
  Rx
  Tx
  Multiwii Flight
  Controller

custom parts:
  MPU-6050 Board GY-521: Acelerometro y Giroscopio MPU-6050 Board GY-521
